# Fritzing sketch Domotica Sketch (saved by Fritzing 0.9.3b)
breadboards: 1

parts:
  Componente1 = Arduino Uno (Rev3)
  Componente2 = Bluetooth HC-05 Macho
  LED1 = LED - 5mm [color="Red (633nm)" package="5 mm [THT]"]
  LED2 = LED - 5mm [color="Red (633nm)" package="5 mm [THT]"]
  LED3 = LED - 5mm [color="Red (633nm)" package="5 mm [THT]"]
  LED4 = LED - 5mm [color="Red (633nm)" package="5 mm [THT]"]
  LED5 = LED - 5mm [color="Red (633nm)" package="5 mm [THT]"]
  LED6 = LED - 5mm [color="Red (633nm)" package="5 mm [THT]"]
  LED7 = LED - 5mm [color="Red (633nm)" package="5 mm [THT]"]
  LED8 = LED - 5mm [color="Red (633nm)" package="5 mm [THT]"]
  LED9 = LED - 5mm [color="Red (633nm)" package="5 mm [THT]"]
  LED10 = LED - 5mm [color="Red (633nm)" package="5 mm [THT]"]
  LED11 = LED - 5mm [color="Red (633nm)" package="5 mm [THT]"]
  LED12 = LED - 5mm [color="Red (633nm)" package="5 mm [THT]"]
  OMRON1 = OMRON PCB Power Relay – G5LE [part_number="G5LE-1\n" package=THT]
  VCC1 = Battery block 9V
  U1 = Vibration Motor- ROB-08449 [package=vibe-motor-10mm]

nets:
  N1: Componente1.D8, LED6.cathode
  N2: Componente1.D9_PWM, LED5.cathode
  N3: Componente1.D10_PWM/SS, LED4.cathode
  N4: Componente1.D11_PWM/MOSI, LED3.cathode
  N5: Componente1.D12/MISO, LED2.cathode
  N6: Componente1.D13/SCK, LED1.cathode
  GND: Componente1.GND, Componente2.GND, LED1.anode, LED2.anode, LED3.anode, LED4.anode, LED5.anode, LED6.anode, LED7.anode, LED8.anode, LED9.anode, LED10.anode, LED11.anode, LED12.anode, OMRON1.COIL2
  N7: Componente1.D0/RX, Componente2.RXD
  N8: Componente1.D1/TX, Componente2.TXD
  N9: Componente1.D2, LED12.cathode, OMRON1.COIL1
  N10: Componente1.D3_PWM, LED11.cathode
  N11: Componente1.D4, LED10.cathode
  N12: Componente1.D5_PWM, LED9.cathode
  N13: Componente1.D6_PWM, LED8.cathode
  N14: Componente1.D7, LED7.cathode
  5V: Componente1.5V, Componente2.VCC
  N15: OMRON1.C, VCC1.+
  N16: OMRON1.B, U1.-
  N17: VCC1.-, U1.+

notes:
  por fines de visual, los Led estan conectados inverso, pero, Cada ¨pin¨va a el positivo del LED, y el Negativo a GND
